# Fritzing sketch fm_radio (saved by Fritzing 0.9.3b)
circuit board: 17.3233cm x 6.09443cm
breadboards: 1

parts:
  Part1 = Arduino Nano (Rev3.0) (ICSP)
  S1 = Pushbutton [package="[THT]"]
  S2 = Pushbutton [package="[THT]"]
  SP1 = SPEAKER [package=pcb_mount_speaker]
  SP2 = SPEAKER [package=pcb_mount_speaker]
  LM386 = Pololu A4988 [package=SO16]
  Ka2284 = Pololu A4988 [package=SO16]
  ANT1 = Antenna
  Grove1 = Grove OLED 128x96 [part_number="SSD1306 LCD"]  # not connected
  TEA5767 = Pololu A4988 [package=SO16]

nets (from the pcb view):
  N1: Part1.GND, LM386.power_in_Ground, LM386.DIR, Ka2284.power_in_Ground, Ka2284.DIR, TEA5767.power_in_Ground, TEA5767.DIR
  N2: Part1.D11/MOSI, S1.Pin_1, S1.Pin_2
  N3: Part1.D12/MISO, S2.Pin_1, S2.Pin_2
  N4: Part1.5V, Part1.A5, Part1.A4, LM386.LM_386_module, LM386.Speaker_out_+, LM386.Speaker_out_-, LM386.Audio_in, LM386.Power_+_5-12V, Ka2284.Power_+_5-12V, TEA5767.TEA5767, TEA5767.SCLOCK_to_A5, TEA5767.SDATA_to_A4, TEA5767.Audio_in, TEA5767.Power_+_5-12V
  N5: S1.Pin_3, S1.Pin_4, S2.Pin_3, S2.Pin_4
  N6: SP1.-, SP2.-
  N7: LM386.Audio_in_ground, TEA5767.Audio_in_ground
  N8: LM386.GND, LM386.connector9
  N9: LM386.connector12, LM386.connector13, LM386.connector14, LM386.connector15
  N10: Ka2284.LM_386_module, Ka2284.Speaker_out_+, Ka2284.Speaker_out_-, Ka2284.Audio_in
  N11: Ka2284.GND, Ka2284.connector9
  N12: Ka2284.connector12, Ka2284.connector13, Ka2284.connector14, Ka2284.connector15
  N13: ANT1.antenna_lead, TEA5767.GND, TEA5767.Ant_out
  N14: TEA5767.connector12, TEA5767.connector13, TEA5767.connector14, TEA5767.connector15

custom parts:
  Pololu A4988: The A4988 stepper motor driver carrier is a breakout board for Allegro’s A4988 microstepping bipolar stepper motor driver. The driver features adjustable current limiting, overcurrent and overtemperature protection, and five different microstep resolutions (down to 1/16-step). It operates from 8 – 35 V and can deliver up to approximately 1 A per phase without a heat sink or forced air flow (it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
  Pololu A4988: The A4988 stepper motor driver carrier is a breakout board for Allegro’s A4988 microstepping bipolar stepper motor driver. The driver features adjustable current limiting, overcurrent and overtemperature protection, and five different microstep resolutions (down to 1/16-step). It operates from 8 – 35 V and can deliver up to approximately 1 A per phase without a heat sink or forced air flow (it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
