# Fritzing sketch fm_radio (saved by Fritzing 0.9.3b)
circuit board: 17.3233cm x 6.09443cm
breadboards: 1

parts:
  Part1 = Arduino Nano (Rev3.0) (ICSP)
  Nokia_5110_LCD_Module3 = Nokia5110 84x48
  S1 = Pushbutton [package="[THT]"]
  S2 = Pushbutton [package="[THT]"]
  S3 = SPST Switch [package=switch-spdt_lock.007s]
  SP1 = SPEAKER [package=pcb_mount_speaker]
  SP2 = SPEAKER [package=pcb_mount_speaker]
  LM386 = Pololu A4988 [package=SO16]
  Ka2284 = Pololu A4988 [package=SO16]
  ANT1 = Antenna
  TEA5767 = Pololu A4988 [package=SO16]
  R1 = Resistor [tolerance=±5% resistance=220 package="0805 [SMD]"]

nets:
  GND: Part1.GND, Nokia_5110_LCD_Module3.Gnd, S1.Pin_3, S1.Pin_4, S2.Pin_3, S2.Pin_4, LM386.power_in_Ground, LM386.DIR, Ka2284.power_in_Ground, Ka2284.DIR, TEA5767.power_in_Ground, TEA5767.DIR
  N1: Part1.D6, Nokia_5110_LCD_Module3.RST
  N2: Part1.D7, Nokia_5110_LCD_Module3.Din_(MOSI)
  N3: Part1.D8, Nokia_5110_LCD_Module3.DC, R1.Pin_0
  N4: Part1.D9, Nokia_5110_LCD_Module3.CE
  N5: Part1.D10, Nokia_5110_LCD_Module3.SCLK
  N6: Part1.D11/MOSI, S1.Pin_1, S1.Pin_2
  N7: Part1.D12/MISO, S2.Pin_1, S2.Pin_2
  5V: Part1.5V, Part1.A5, Part1.A4, Nokia_5110_LCD_Module3.Vcc, S3.S, LM386.LM_386_module, LM386.Speaker_out_+, LM386.Speaker_out_-, LM386.Audio_in, LM386.Power_+_5-12V, Ka2284.Power_+_5-12V, TEA5767.TEA5767, TEA5767.SDA, TEA5767.SCLk-, TEA5767.Audio_in, TEA5767.Power_+_5-12V
  N8: S3.P, R1.Pin_1
  N9: SP1.-, SP2.-
  N10: LM386.Audio_in_ground, TEA5767.Audio_in_ground
  N11: LM386.GND, LM386.connector9
  N12: LM386.connector12, LM386.connector13, LM386.connector14, LM386.connector15
  N13: Ka2284.LM_386_module, Ka2284.Speaker_out_+, Ka2284.Speaker_out_-, Ka2284.Audio_in
  N14: Ka2284.GND, Ka2284.connector9
  N15: Ka2284.connector12, Ka2284.connector13, Ka2284.connector14, Ka2284.connector15
  N16: ANT1.antenna_lead, TEA5767.GND, TEA5767.Ant_out
  N17: TEA5767.connector12, TEA5767.connector13, TEA5767.connector14, TEA5767.connector15

custom parts:
  : Nokia 5110 LCD with 8 pin. It's a 45mm*45mm module part. Description: The Nokia 5110 is a basic graphic LCD screen for lots of applications. It was originally intended for as a cell phone screen. This one is mounted on an easy to solder PCB. It uses the PCD8544 controller. The PCD8544 is a low power CMOS LCD controller/driver, designed to drive a graphic display of 48 rows and 84 columns. All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
  Pololu A4988: The A4988 stepper motor driver carrier is a breakout board for Allegro’s A4988 microstepping bipolar stepper motor driver. The driver features adjustable current limiting, overcurrent and overtemperature protection, and five different microstep resolutions (down to 1/16-step). It operates from 8 – 35 V and can deliver up to approximately 1 A per phase without a heat sink or forced air flow (it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
  Pololu A4988: The A4988 stepper motor driver carrier is a breakout board for Allegro’s A4988 microstepping bipolar stepper motor driver. The driver features adjustable current limiting, overcurrent and overtemperature protection, and five different microstep resolutions (down to 1/16-step). It operates from 8 – 35 V and can deliver up to approximately 1 A per phase without a heat sink or forced air flow (it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
